# Fritzing sketch accelerometer (saved by Fritzing 0.9.3b)

parts:
  Componente3 = Triple Axis Accelerometer Breakout - ADXL335
  Componente4 = Arduino Nano (Rev3.0)

nets:
  N1: Componente3.ZOUT, Componente4.A3
  N2: Componente3.YOUT, Componente4.A2
  N3: Componente3.XOUT, Componente4.A1
  GND: Componente3.GND, Componente4.GND
  VCC: Componente3.VCC, Componente4.3V3
